// Logisim project CSE332.9-1421353042-Md. Sayadul Haque-Project Part 2-32-bit Single cycle CPU with control.circ as structural Verilog
// ALU
module _2_bit_ALU (
  input  [1:0] A,
  input  A_invert,
  input  [1:0] B,
  input  B_invert,
  input  [2:0] Select_Bits,
  input  Carry_in,
  output [1:0] Output,
  output Carry_Out
);

  wire adder_1_cout;
  wire [1:0] adder_1_out, and_1_out, multiplexer_1_out, multiplexer_2_out, not_1_out, not_2_out, or_1_out,
       xor_1_out;

  assign not_1_out = ~A;  // NOT_Gate not_1, 2 bits wide
  assign not_2_out = ~B;  // NOT_Gate not_2, 2 bits wide
  Multiplexer #(.width(2), .enable("false")) multiplexer_1 (
    .in0(A), .in1(not_1_out), .out(multiplexer_1_out), .sel(A_invert));
  Multiplexer #(.width(2), .enable("false")) multiplexer_2 (
    .in0(B), .in1(not_2_out), .out(multiplexer_2_out), .sel(B_invert));
  Adder #(.width(2)) adder_1 (.a(A), .b(multiplexer_2_out), .out(adder_1_out), .cin(Carry_in), .cout(adder_1_cout));
  assign and_1_out = multiplexer_1_out & multiplexer_2_out;  // AND_Gate and_1, 2 bits wide
  assign or_1_out = multiplexer_1_out | multiplexer_2_out;  // OR_Gate or_1, 2 bits wide
  assign xor_1_out = multiplexer_1_out ^ multiplexer_2_out;  // XOR_Gate xor_1, 2 bits wide
  Multiplexer #(.select(3), .width(2), .enable("false")) multiplexer_3 (
    .in0(and_1_out), .in1(or_1_out), .in2(adder_1_out), .in3(and_1_out), .in4(or_1_out), .in5(xor_1_out),
    .in6(adder_1_out), .in7(2'b00), .out(Output), .sel(Select_Bits));
  Multiplexer #(.select(3), .enable("false")) multiplexer_4 (
    .in0(1'b0), .in1(1'b0), .in2(adder_1_cout), .in3(1'b0), .in4(1'b0), .in5(1'b0), .in6(adder_1_cout),
    .in7(1'b0), .out(Carry_Out), .sel(Select_Bits));
endmodule

// ALU
module _4_bit_ALU (
  input  B_invet,
  input  A_invert,
  input  [3:0] A,
  input  [3:0] B,
  input  Carry_in,
  input  [2:0] Select_Bits,
  output [3:0] Output,
  output Carry_out
);

  wire _1_carry_out;

  _2_bit_ALU _1 (
    .A(A[1:0]), .B(B[1:0]), .Select_Bits(Select_Bits), .Output(Output[1:0]), .Carry_Out(_1_carry_out),
    .Carry_in(Carry_in), .A_invert(A_invert), .B_invert(B_invet));
  _2_bit_ALU _2 (
    .A(A[3:2]), .B(B[3:2]), .Select_Bits(Select_Bits), .Output(Output[3:2]), .Carry_Out(Carry_out),
    .Carry_in(_1_carry_out), .A_invert(A_invert), .B_invert(B_invet));
endmodule

// ALU
module _8_bit_ALU (
  input  [7:0] A,
  input  A_invert,
  input  B_invert,
  input  [7:0] B,
  input  Carry_in,
  input  [2:0] Select_Bits,
  output [7:0] Output,
  output Carry_out
);

  wire _1_carry_out;

  _4_bit_ALU _1 (
    .A(A[3:0]), .B(B[3:0]), .Carry_in(Carry_in), .Select_Bits(Select_Bits), .Output(Output[3:0]),
    .Carry_out(_1_carry_out), .B_invet(B_invert), .A_invert(A_invert));
  _4_bit_ALU _2 (
    .A(A[7:4]), .B(B[7:4]), .Carry_in(_1_carry_out), .Select_Bits(Select_Bits), .Output(Output[7:4]),
    .Carry_out(Carry_out), .B_invet(B_invert), .A_invert(A_invert));
endmodule

// ALU
module _16_bit_ALU (
  input  [15:0] A,
  input  A_invert,
  input  B_invert,
  input  [15:0] B,
  input  Carry_in,
  input  [2:0] Select_Bits,
  output [15:0] Output,
  output Carry_out
);

  wire _1_carry_out;

  _8_bit_ALU _1 (
    .A(A[7:0]), .B(B[7:0]), .Carry_in(Carry_in), .Select_Bits(Select_Bits), .Output(Output[7:0]),
    .Carry_out(_1_carry_out), .B_invert(B_invert), .A_invert(A_invert));
  _8_bit_ALU _2 (
    .A(A[15:8]), .B(B[15:8]), .Carry_in(_1_carry_out), .Select_Bits(Select_Bits), .Output(Output[15:8]),
    .Carry_out(Carry_out), .B_invert(B_invert), .A_invert(A_invert));
endmodule

// ALU
module _32_bit_ALU (
  input  B_invert,
  input  A_invert,
  input  [31:0] A,
  input  [31:0] B,
  input  Carry_in,
  input  [2:0] Select_Bits,
  output [31:0] Output,
  output Carry_out
);

  wire _1_p7;

  // _16_bit_ALU _1: pin names not known; wires that end beside it: A[15:0], A_invert, B_invert, B[15:0], Select_Bits, Carry_in, _1_p7, Output[15:0]
  _16_bit_ALU _2 (
    .A(A[31:16]), .B(B[31:16]), .Carry_in(_1_p7), .Select_Bits(Select_Bits), .Output(Output[31:16]),
    .Carry_out(Carry_out), .A_invert(A_invert), .B_invert(B_invert));
endmodule

module _4_Bit_by_4_Bit_Multiplication_Unit (
  input  [3:0] Multiplier,
  input  [3:0] Multiplicand,
  output [7:0] S
);

  wire [2:0] and_9_out;
  wire [3:0] adder_1_out, and_3_out, and_4_out, and_7_out;
  wire [3:1] adder_2_out;
  wire [3:3] adder_2_cout;

  and and_1 (S[0], Multiplicand[0], Multiplier[0]);
  and and_2 (and_3_out[1], Multiplier[1], Multiplicand[1]);
  and and_3 (and_3_out[0], Multiplicand[0], Multiplier[1]);
  and and_4 (and_4_out[0], Multiplicand[0], Multiplier[2]);
  and and_5 (and_4_out[1], Multiplicand[1], Multiplier[2]);
  and and_6 (and_7_out[1], Multiplicand[1], Multiplier[3]);
  and and_7 (and_7_out[0], Multiplicand[0], Multiplier[3]);
  and and_8 (and_9_out[1], Multiplier[0], Multiplicand[2]);
  and and_9 (and_9_out[0], Multiplier[0], Multiplicand[1]);
  and and_10 (and_3_out[2], Multiplicand[2], Multiplier[1]);
  and and_11 (and_4_out[2], Multiplicand[2], Multiplier[2]);
  and and_12 (and_7_out[2], Multiplicand[2], Multiplier[3]);
  and and_13 (and_9_out[2], Multiplier[0], Multiplicand[3]);
  and and_14 (and_3_out[3], Multiplicand[3], Multiplier[1]);
  and and_15 (and_4_out[3], Multiplicand[3], Multiplier[2]);
  and and_16 (and_7_out[3], Multiplicand[3], Multiplier[3]);
  Adder #(.width(4)) adder_1 (
    .a({1'b0, and_9_out}), .b(and_3_out), .out({adder_1_out[2:0], S[1]}), .cin(1'b0), .cout(adder_1_out[3]));
  Adder #(.width(4)) adder_2 (
    .a(adder_1_out), .b(and_4_out), .out({adder_2_out, S[2]}), .cin(1'b0), .cout(adder_2_cout[3]));
  Adder #(.width(4)) adder_3 (.a({adder_2_cout[3], adder_2_out}), .b(and_7_out), .out(S[6:3]), .cin(1'b0), .cout(S[7]));
endmodule

// Multiplication Unit
module _16_bit_by_16_bit_Multiplication_Unit (
  input  [15:0] Multiplicand,
  input  [15:0] Multiplier,
  output [31:0] Output
);

  wire [14:0] Adder_1_1, adder_4_out, adder_7_out, adder_11_out, adder_13_out, adder_14_out, adder_15_out;
  wire [15:0] Adder_1_2, adder_1_cout, Adder_2_2, adder_2_cout, Adder_3_2, adder_3_cout, Adder_4_2,
       Adder_5_2, Adder_6_2, adder_6_cout, Adder_7_2, Adder_8_2, adder_8_cout, Adder_9_2, adder_9_cout,
       Adder_10_2, adder_10_cout, Adder_11_2, Adder_12_2, adder_12_cout, Adder_13_2, Adder_14_2, Adder_15_2;
  wire [15:15] adder_4_cout, adder_7_cout, adder_11_cout, adder_13_cout, adder_14_cout, adder_15_cout;

  and and_1 (Adder_9_2[15], Multiplicand[15], Multiplier[9]);
  and and_2 (Adder_10_2[15], Multiplicand[15], Multiplier[10]);
  and and_3 (Adder_11_2[15], Multiplicand[15], Multiplier[11]);
  and and_4 (Adder_12_2[15], Multiplicand[15], Multiplier[12]);
  and and_5 (Adder_13_2[14], Multiplicand[14], Multiplier[13]);
  and and_6 (Adder_13_2[15], Multiplicand[15], Multiplier[13]);
  and and_7 (Adder_14_2[14], Multiplicand[14], Multiplier[14]);
  and and_8 (Adder_14_2[15], Multiplicand[15], Multiplier[14]);
  and and_9 (Adder_15_2[15], Multiplicand[15], Multiplier[15]);
  and and_10 (Adder_15_2[14], Multiplicand[14], Multiplier[15]);
  and and_11 (Adder_1_2[15], Multiplicand[15], Multiplier[1]);
  and and_12 (Adder_2_2[15], Multiplicand[15], Multiplier[2]);
  and and_13 (Adder_3_2[15], Multiplicand[15], Multiplier[3]);
  and and_14 (Adder_4_2[15], Multiplicand[15], Multiplier[4]);
  and and_15 (Adder_5_2[14], Multiplicand[14], Multiplier[5]);
  and and_16 (Adder_5_2[15], Multiplicand[15], Multiplier[5]);
  and and_17 (Adder_6_2[14], Multiplicand[14], Multiplier[6]);
  and and_18 (Adder_6_2[15], Multiplicand[15], Multiplier[6]);
  and and_19 (Adder_7_2[14], Multiplicand[14], Multiplier[7]);
  and and_20 (Adder_7_2[15], Multiplicand[15], Multiplier[7]);
  and and_21 (Adder_8_2[15], Multiplicand[15], Multiplier[8]);
  and and_22 (Adder_8_2[14], Multiplicand[14], Multiplier[8]);
  and and_23 (Adder_9_2[13], Multiplicand[13], Multiplier[9]);
  and and_24 (Adder_9_2[14], Multiplicand[14], Multiplier[9]);
  and and_25 (Adder_10_2[13], Multiplicand[13], Multiplier[10]);
  and and_26 (Adder_10_2[14], Multiplicand[14], Multiplier[10]);
  and and_27 (Adder_11_2[13], Multiplicand[13], Multiplier[11]);
  and and_28 (Adder_11_2[14], Multiplicand[14], Multiplier[11]);
  and and_29 (Adder_12_2[13], Multiplicand[13], Multiplier[12]);
  and and_30 (Adder_12_2[14], Multiplicand[14], Multiplier[12]);
  and and_31 (Adder_13_2[12], Multiplicand[12], Multiplier[13]);
  and and_32 (Adder_13_2[13], Multiplicand[13], Multiplier[13]);
  and and_33 (Adder_14_2[12], Multiplicand[12], Multiplier[14]);
  and and_34 (Adder_14_2[13], Multiplicand[13], Multiplier[14]);
  and and_35 (Adder_15_2[13], Multiplicand[13], Multiplier[15]);
  and and_36 (Adder_15_2[12], Multiplicand[12], Multiplier[15]);
  and and_37 (Adder_1_1[13], Multiplicand[14], Multiplier[0]);
  and and_38 (Adder_1_1[14], Multiplicand[15], Multiplier[0]);
  and and_39 (Adder_1_2[13], Multiplicand[13], Multiplier[1]);
  and and_40 (Adder_1_2[14], Multiplicand[14], Multiplier[1]);
  and and_41 (Adder_2_2[14], Multiplicand[14], Multiplier[2]);
  and and_42 (Adder_2_2[13], Multiplicand[13], Multiplier[2]);
  and and_43 (Adder_3_2[13], Multiplicand[13], Multiplier[3]);
  and and_44 (Adder_3_2[14], Multiplicand[14], Multiplier[3]);
  and and_45 (Adder_4_2[14], Multiplicand[14], Multiplier[4]);
  and and_46 (Adder_4_2[13], Multiplicand[13], Multiplier[4]);
  and and_47 (Adder_5_2[12], Multiplicand[12], Multiplier[5]);
  and and_48 (Adder_5_2[13], Multiplicand[13], Multiplier[5]);
  and and_49 (Adder_6_2[13], Multiplicand[13], Multiplier[6]);
  and and_50 (Adder_6_2[12], Multiplicand[12], Multiplier[6]);
  and and_51 (Adder_7_2[12], Multiplicand[12], Multiplier[7]);
  and and_52 (Adder_7_2[13], Multiplicand[13], Multiplier[7]);
  and and_53 (Adder_8_2[13], Multiplicand[13], Multiplier[8]);
  and and_54 (Adder_8_2[12], Multiplicand[12], Multiplier[8]);
  and and_55 (Adder_9_2[12], Multiplicand[12], Multiplier[9]);
  and and_56 (Adder_9_2[11], Multiplicand[11], Multiplier[9]);
  and and_57 (Adder_10_2[11], Multiplicand[11], Multiplier[10]);
  and and_58 (Adder_10_2[12], Multiplicand[12], Multiplier[10]);
  and and_59 (Adder_11_2[11], Multiplicand[11], Multiplier[11]);
  and and_60 (Adder_11_2[12], Multiplicand[12], Multiplier[11]);
  and and_61 (Adder_12_2[12], Multiplicand[12], Multiplier[12]);
  and and_62 (Adder_12_2[11], Multiplicand[11], Multiplier[12]);
  and and_63 (Adder_13_2[11], Multiplicand[11], Multiplier[13]);
  and and_64 (Adder_13_2[10], Multiplicand[10], Multiplier[13]);
  and and_65 (Adder_14_2[11], Multiplicand[11], Multiplier[14]);
  and and_66 (Adder_14_2[10], Multiplicand[10], Multiplier[14]);
  and and_67 (Adder_15_2[10], Multiplicand[10], Multiplier[15]);
  and and_68 (Adder_15_2[11], Multiplicand[11], Multiplier[15]);
  and and_69 (Adder_1_1[12], Multiplicand[13], Multiplier[0]);
  and and_70 (Adder_1_1[11], Multiplicand[12], Multiplier[0]);
  and and_71 (Adder_1_2[12], Multiplicand[12], Multiplier[1]);
  and and_72 (Adder_1_2[11], Multiplicand[11], Multiplier[1]);
  and and_73 (Adder_2_2[12], Multiplicand[12], Multiplier[2]);
  and and_74 (Adder_2_2[11], Multiplicand[11], Multiplier[2]);
  and and_75 (Adder_3_2[12], Multiplicand[12], Multiplier[3]);
  and and_76 (Adder_3_2[11], Multiplicand[11], Multiplier[3]);
  and and_77 (Adder_4_2[12], Multiplicand[12], Multiplier[4]);
  and and_78 (Adder_4_2[11], Multiplicand[11], Multiplier[4]);
  and and_79 (Adder_5_2[10], Multiplicand[10], Multiplier[5]);
  and and_80 (Adder_5_2[11], Multiplicand[11], Multiplier[5]);
  and and_81 (Adder_6_2[11], Multiplicand[11], Multiplier[6]);
  and and_82 (Adder_6_2[10], Multiplicand[10], Multiplier[6]);
  and and_83 (Adder_7_2[11], Multiplicand[11], Multiplier[7]);
  and and_84 (Adder_7_2[10], Multiplicand[10], Multiplier[7]);
  and and_85 (Adder_8_2[11], Multiplicand[11], Multiplier[8]);
  and and_86 (Adder_8_2[10], Multiplicand[10], Multiplier[8]);
  and and_87 (Adder_9_2[10], Multiplicand[10], Multiplier[9]);
  and and_88 (Adder_9_2[9], Multiplicand[9], Multiplier[9]);
  and and_89 (Adder_10_2[9], Multiplicand[9], Multiplier[10]);
  and and_90 (Adder_10_2[10], Multiplicand[10], Multiplier[10]);
  and and_91 (Adder_11_2[10], Multiplicand[10], Multiplier[11]);
  and and_92 (Adder_11_2[9], Multiplicand[9], Multiplier[11]);
  and and_93 (Adder_12_2[10], Multiplicand[10], Multiplier[12]);
  and and_94 (Adder_12_2[9], Multiplicand[9], Multiplier[12]);
  and and_95 (Adder_13_2[8], Multiplicand[8], Multiplier[13]);
  and and_96 (Adder_13_2[9], Multiplicand[9], Multiplier[13]);
  and and_97 (Adder_14_2[8], Multiplicand[8], Multiplier[14]);
  and and_98 (Adder_14_2[9], Multiplicand[9], Multiplier[14]);
  and and_99 (Adder_15_2[9], Multiplicand[9], Multiplier[15]);
  and and_100 (Adder_15_2[8], Multiplicand[8], Multiplier[15]);
  and and_101 (Adder_1_1[9], Multiplicand[10], Multiplier[0]);
  and and_102 (Adder_1_1[10], Multiplicand[11], Multiplier[0]);
  and and_103 (Adder_1_2[9], Multiplicand[9], Multiplier[1]);
  and and_104 (Adder_1_2[10], Multiplicand[10], Multiplier[1]);
  and and_105 (Adder_2_2[10], Multiplicand[10], Multiplier[2]);
  and and_106 (Adder_2_2[9], Multiplicand[9], Multiplier[2]);
  and and_107 (Adder_3_2[10], Multiplicand[10], Multiplier[3]);
  and and_108 (Adder_3_2[9], Multiplicand[9], Multiplier[3]);
  and and_109 (Adder_4_2[9], Multiplicand[9], Multiplier[4]);
  and and_110 (Adder_4_2[10], Multiplicand[10], Multiplier[4]);
  and and_111 (Adder_5_2[9], Multiplicand[9], Multiplier[5]);
  and and_112 (Adder_5_2[8], Multiplicand[8], Multiplier[5]);
  and and_113 (Adder_6_2[8], Multiplicand[8], Multiplier[6]);
  and and_114 (Adder_6_2[9], Multiplicand[9], Multiplier[6]);
  and and_115 (Adder_7_2[9], Multiplicand[9], Multiplier[7]);
  and and_116 (Adder_7_2[8], Multiplicand[8], Multiplier[7]);
  and and_117 (Adder_8_2[9], Multiplicand[9], Multiplier[8]);
  and and_118 (Adder_8_2[8], Multiplicand[8], Multiplier[8]);
  and and_119 (Adder_9_2[8], Multiplicand[8], Multiplier[9]);
  and and_120 (Adder_9_2[7], Multiplicand[7], Multiplier[9]);
  and and_121 (Adder_10_2[7], Multiplicand[7], Multiplier[10]);
  and and_122 (Adder_10_2[8], Multiplicand[8], Multiplier[10]);
  and and_123 (Adder_11_2[8], Multiplicand[8], Multiplier[11]);
  and and_124 (Adder_11_2[7], Multiplicand[7], Multiplier[11]);
  and and_125 (Adder_12_2[7], Multiplicand[7], Multiplier[12]);
  and and_126 (Adder_12_2[8], Multiplicand[8], Multiplier[12]);
  and and_127 (Adder_13_2[6], Multiplicand[6], Multiplier[13]);
  and and_128 (Adder_13_2[7], Multiplicand[7], Multiplier[13]);
  and and_129 (Adder_14_2[6], Multiplicand[6], Multiplier[14]);
  and and_130 (Adder_14_2[7], Multiplicand[7], Multiplier[14]);
  and and_131 (Adder_15_2[6], Multiplicand[6], Multiplier[15]);
  and and_132 (Adder_15_2[7], Multiplicand[7], Multiplier[15]);
  and and_133 (Adder_1_1[7], Multiplicand[8], Multiplier[0]);
  and and_134 (Adder_1_1[8], Multiplicand[9], Multiplier[0]);
  and and_135 (Adder_1_2[8], Multiplicand[8], Multiplier[1]);
  and and_136 (Adder_1_2[7], Multiplicand[7], Multiplier[1]);
  and and_137 (Adder_2_2[7], Multiplicand[7], Multiplier[2]);
  and and_138 (Adder_2_2[8], Multiplicand[8], Multiplier[2]);
  and and_139 (Adder_3_2[7], Multiplicand[7], Multiplier[3]);
  and and_140 (Adder_3_2[8], Multiplicand[8], Multiplier[3]);
  and and_141 (Adder_4_2[7], Multiplicand[7], Multiplier[4]);
  and and_142 (Adder_4_2[8], Multiplicand[8], Multiplier[4]);
  and and_143 (Adder_5_2[6], Multiplicand[6], Multiplier[5]);
  and and_144 (Adder_5_2[7], Multiplicand[7], Multiplier[5]);
  and and_145 (Adder_6_2[7], Multiplicand[7], Multiplier[6]);
  and and_146 (Adder_6_2[6], Multiplicand[6], Multiplier[6]);
  and and_147 (Adder_7_2[6], Multiplicand[6], Multiplier[7]);
  and and_148 (Adder_7_2[7], Multiplicand[7], Multiplier[7]);
  and and_149 (Adder_8_2[6], Multiplicand[6], Multiplier[8]);
  and and_150 (Adder_8_2[7], Multiplicand[7], Multiplier[8]);
  and and_151 (Adder_9_2[5], Multiplicand[5], Multiplier[9]);
  and and_152 (Adder_9_2[6], Multiplicand[6], Multiplier[9]);
  and and_153 (Adder_10_2[6], Multiplicand[6], Multiplier[10]);
  and and_154 (Adder_10_2[5], Multiplicand[5], Multiplier[10]);
  and and_155 (Adder_11_2[5], Multiplicand[5], Multiplier[11]);
  and and_156 (Adder_11_2[6], Multiplicand[6], Multiplier[11]);
  and and_157 (Adder_12_2[5], Multiplicand[5], Multiplier[12]);
  and and_158 (Adder_12_2[6], Multiplicand[6], Multiplier[12]);
  and and_159 (Adder_13_2[4], Multiplicand[4], Multiplier[13]);
  and and_160 (Adder_13_2[5], Multiplicand[5], Multiplier[13]);
  and and_161 (Adder_14_2[4], Multiplicand[4], Multiplier[14]);
  and and_162 (Adder_14_2[5], Multiplicand[5], Multiplier[14]);
  and and_163 (Adder_15_2[5], Multiplicand[5], Multiplier[15]);
  and and_164 (Adder_15_2[4], Multiplicand[4], Multiplier[15]);
  and and_165 (Adder_1_1[5], Multiplicand[6], Multiplier[0]);
  and and_166 (Adder_1_1[6], Multiplicand[7], Multiplier[0]);
  and and_167 (Adder_1_2[6], Multiplicand[6], Multiplier[1]);
  and and_168 (Adder_1_2[5], Multiplicand[5], Multiplier[1]);
  and and_169 (Adder_2_2[5], Multiplicand[5], Multiplier[2]);
  and and_170 (Adder_2_2[6], Multiplicand[6], Multiplier[2]);
  and and_171 (Adder_3_2[6], Multiplicand[6], Multiplier[3]);
  and and_172 (Adder_3_2[5], Multiplicand[5], Multiplier[3]);
  and and_173 (Adder_4_2[5], Multiplicand[5], Multiplier[4]);
  and and_174 (Adder_4_2[6], Multiplicand[6], Multiplier[4]);
  and and_175 (Adder_5_2[5], Multiplicand[5], Multiplier[5]);
  and and_176 (Adder_5_2[4], Multiplicand[4], Multiplier[5]);
  and and_177 (Adder_6_2[5], Multiplicand[5], Multiplier[6]);
  and and_178 (Adder_6_2[4], Multiplicand[4], Multiplier[6]);
  and and_179 (Adder_7_2[5], Multiplicand[5], Multiplier[7]);
  and and_180 (Adder_7_2[4], Multiplicand[4], Multiplier[7]);
  and and_181 (Adder_8_2[5], Multiplicand[5], Multiplier[8]);
  and and_182 (Adder_8_2[4], Multiplicand[4], Multiplier[8]);
  and and_183 (Adder_9_2[4], Multiplicand[4], Multiplier[9]);
  and and_184 (Adder_9_2[3], Multiplicand[3], Multiplier[9]);
  and and_185 (Adder_10_2[3], Multiplicand[3], Multiplier[10]);
  and and_186 (Adder_10_2[4], Multiplicand[4], Multiplier[10]);
  and and_187 (Adder_11_2[4], Multiplicand[4], Multiplier[11]);
  and and_188 (Adder_11_2[3], Multiplicand[3], Multiplier[11]);
  and and_189 (Adder_12_2[3], Multiplicand[3], Multiplier[12]);
  and and_190 (Adder_12_2[4], Multiplicand[4], Multiplier[12]);
  and and_191 (Adder_13_2[3], Multiplicand[3], Multiplier[13]);
  and and_192 (Adder_13_2[2], Multiplicand[2], Multiplier[13]);
  and and_193 (Adder_14_2[2], Multiplicand[2], Multiplier[14]);
  and and_194 (Adder_14_2[3], Multiplicand[3], Multiplier[14]);
  and and_195 (Adder_15_2[3], Multiplicand[3], Multiplier[15]);
  and and_196 (Adder_15_2[2], Multiplicand[2], Multiplier[15]);
  and and_197 (Adder_1_1[3], Multiplicand[4], Multiplier[0]);
  and and_198 (Adder_1_1[4], Multiplicand[5], Multiplier[0]);
  and and_199 (Adder_1_2[3], Multiplicand[3], Multiplier[1]);
  and and_200 (Adder_1_2[4], Multiplicand[4], Multiplier[1]);
  and and_201 (Adder_2_2[4], Multiplicand[4], Multiplier[2]);
  and and_202 (Adder_2_2[3], Multiplicand[3], Multiplier[2]);
  and and_203 (Adder_3_2[3], Multiplicand[3], Multiplier[3]);
  and and_204 (Adder_3_2[4], Multiplicand[4], Multiplier[3]);
  and and_205 (Adder_4_2[3], Multiplicand[3], Multiplier[4]);
  and and_206 (Adder_4_2[4], Multiplicand[4], Multiplier[4]);
  and and_207 (Adder_5_2[2], Multiplicand[2], Multiplier[5]);
  and and_208 (Adder_5_2[3], Multiplicand[3], Multiplier[5]);
  and and_209 (Adder_6_2[3], Multiplicand[3], Multiplier[6]);
  and and_210 (Adder_6_2[2], Multiplicand[2], Multiplier[6]);
  and and_211 (Adder_7_2[3], Multiplicand[3], Multiplier[7]);
  and and_212 (Adder_7_2[2], Multiplicand[2], Multiplier[7]);
  and and_213 (Adder_8_2[2], Multiplicand[2], Multiplier[8]);
  and and_214 (Adder_8_2[3], Multiplicand[3], Multiplier[8]);
  and and_215 (Adder_9_2[2], Multiplicand[2], Multiplier[9]);
  and and_216 (Adder_9_2[1], Multiplicand[1], Multiplier[9]);
  and and_217 (Adder_10_2[2], Multiplicand[2], Multiplier[10]);
  and and_218 (Adder_10_2[1], Multiplicand[1], Multiplier[10]);
  and and_219 (Adder_11_2[2], Multiplicand[2], Multiplier[11]);
  and and_220 (Adder_11_2[1], Multiplicand[1], Multiplier[11]);
  and and_221 (Adder_12_2[1], Multiplicand[1], Multiplier[12]);
  and and_222 (Adder_12_2[2], Multiplicand[2], Multiplier[12]);
  and and_223 (Adder_13_2[0], Multiplicand[0], Multiplier[13]);
  and and_224 (Adder_13_2[1], Multiplicand[1], Multiplier[13]);
  and and_225 (Adder_14_2[1], Multiplicand[1], Multiplier[14]);
  and and_226 (Adder_14_2[0], Multiplicand[0], Multiplier[14]);
  and and_227 (Adder_15_2[0], Multiplicand[0], Multiplier[15]);
  and and_228 (Adder_15_2[1], Multiplicand[1], Multiplier[15]);
  and and_229 (Adder_1_1[1], Multiplicand[2], Multiplier[0]);
  and and_230 (Adder_1_1[2], Multiplicand[3], Multiplier[0]);
  and and_231 (Adder_1_2[2], Multiplicand[2], Multiplier[1]);
  and and_232 (Adder_1_2[1], Multiplicand[1], Multiplier[1]);
  and and_233 (Adder_2_2[1], Multiplicand[1], Multiplier[2]);
  and and_234 (Adder_2_2[2], Multiplicand[2], Multiplier[2]);
  and and_235 (Adder_3_2[1], Multiplicand[1], Multiplier[3]);
  and and_236 (Adder_3_2[2], Multiplicand[2], Multiplier[3]);
  and and_237 (Adder_4_2[2], Multiplicand[2], Multiplier[4]);
  and and_238 (Adder_4_2[1], Multiplicand[1], Multiplier[4]);
  and and_239 (Adder_5_2[0], Multiplicand[0], Multiplier[5]);
  and and_240 (Adder_5_2[1], Multiplicand[1], Multiplier[5]);
  and and_241 (Adder_6_2[0], Multiplicand[0], Multiplier[6]);
  and and_242 (Adder_6_2[1], Multiplicand[1], Multiplier[6]);
  and and_243 (Adder_7_2[1], Multiplicand[1], Multiplier[7]);
  and and_244 (Adder_7_2[0], Multiplicand[0], Multiplier[7]);
  and and_245 (Adder_8_2[0], Multiplicand[0], Multiplier[8]);
  and and_246 (Adder_8_2[1], Multiplicand[1], Multiplier[8]);
  and and_247 (Adder_9_2[0], Multiplicand[0], Multiplier[9]);
  and and_248 (Adder_10_2[0], Multiplicand[0], Multiplier[10]);
  and and_249 (Adder_11_2[0], Multiplicand[0], Multiplier[11]);
  and and_250 (Adder_12_2[0], Multiplicand[0], Multiplier[12]);
  and and_251 (Output[0], Multiplicand[0], Multiplier[0]);
  and and_252 (Adder_1_1[0], Multiplicand[1], Multiplier[0]);
  and and_253 (Adder_1_2[0], Multiplicand[0], Multiplier[1]);
  and and_254 (Adder_2_2[0], Multiplicand[0], Multiplier[2]);
  and and_255 (Adder_3_2[0], Multiplicand[0], Multiplier[3]);
  and and_256 (Adder_4_2[0], Multiplicand[0], Multiplier[4]);
  Adder #(.width(16)) adder_1 (
    .a({adder_15_cout[15], adder_15_out}), .b(Adder_11_2), .out({adder_1_cout[14:0], Output[11]}),
    .cin(1'b0), .cout(adder_1_cout[15]));
  Adder #(.width(16)) adder_2 (
    .a(adder_1_cout), .b(Adder_12_2), .out({adder_2_cout[14:0], Output[12]}), .cin(1'b0),
    .cout(adder_2_cout[15]));
  Adder #(.width(16)) adder_3 (
    .a(adder_2_cout), .b(Adder_13_2), .out({adder_3_cout[14:0], Output[13]}), .cin(1'b0),
    .cout(adder_3_cout[15]));
  Adder #(.width(16)) adder_4 (
    .a(adder_3_cout), .b(Adder_14_2), .out({adder_4_out, Output[14]}), .cin(1'b0), .cout(adder_4_cout[15]));
  Adder #(.width(16)) adder_5 (
    .a({adder_4_cout[15], adder_4_out}), .b(Adder_15_2), .out(Output[30:15]), .cin(1'b0), .cout(Output[31]));
  Adder #(.width(16)) adder_6 (
    .a({1'b0, Adder_1_1}), .b(Adder_1_2), .out({adder_6_cout[14:0], Output[1]}), .cin(1'b0),
    .cout(adder_6_cout[15]));
  Adder #(.width(16)) adder_7 (
    .a(adder_6_cout), .b(Adder_2_2), .out({adder_7_out, Output[2]}), .cin(1'b0), .cout(adder_7_cout[15]));
  Adder #(.width(16)) adder_8 (
    .a({adder_7_cout[15], adder_7_out}), .b(Adder_3_2), .out({adder_8_cout[14:0], Output[3]}), .cin(1'b0),
    .cout(adder_8_cout[15]));
  Adder #(.width(16)) adder_9 (
    .a(adder_8_cout), .b(Adder_4_2), .out({adder_9_cout[14:0], Output[4]}), .cin(1'b0),
    .cout(adder_9_cout[15]));
  Adder #(.width(16)) adder_10 (
    .a(adder_9_cout), .b(Adder_5_2), .out({adder_10_cout[14:0], Output[5]}), .cin(1'b0),
    .cout(adder_10_cout[15]));
  Adder #(.width(16)) adder_11 (
    .a(adder_10_cout), .b(Adder_6_2), .out({adder_11_out, Output[6]}), .cin(1'b0), .cout(adder_11_cout[15]));
  Adder #(.width(16)) adder_12 (
    .a({adder_11_cout[15], adder_11_out}), .b(Adder_7_2), .out({adder_12_cout[14:0], Output[7]}), .cin(1'b0),
    .cout(adder_12_cout[15]));
  Adder #(.width(16)) adder_13 (
    .a(adder_12_cout), .b(Adder_8_2), .out({adder_13_out, Output[8]}), .cin(1'b0), .cout(adder_13_cout[15]));
  Adder #(.width(16)) adder_14 (
    .a({adder_13_cout[15], adder_13_out}), .b(Adder_9_2), .out({adder_14_out, Output[9]}), .cin(1'b0),
    .cout(adder_14_cout[15]));
  Adder #(.width(16)) adder_15 (
    .a({adder_14_cout[15], adder_14_out}), .b(Adder_10_2), .out({adder_15_out, Output[10]}), .cin(1'b0),
    .cout(adder_15_cout[15]));

  // Other names for the same wires on the sheet: O14 = Output[13]; O15 = Output[14]; O12 = Output[11];
  //   O13 = Output[12]; O6 = Output[5]; O7 = Output[6]; O8 = Output[7]; O9 = Output[8]; O10 = Output[9];
  //   O11 = Output[10]; O4 = Output[3]; O5 = Output[4]; O3 = Output[2]; _02 = Output[1]; B1 = Multiplicand[0];
  //   B2 = Multiplicand[1]; B3 = Multiplicand[2]; B4 = Multiplicand[3]; B5 = Multiplicand[4]; B6 = Multiplicand[5];
  //   B7 = Multiplicand[6]; B8 = Multiplicand[7]; B9 = Multiplicand[8]; B10 = Multiplicand[9]; B11 = Multiplicand[10];
  //   B12 = Multiplicand[11]; B13 = Multiplicand[12]; B14 = Multiplicand[13]; B15 = Multiplicand[14];
  //   B16 = Multiplicand[15]; A1 = Multiplier[0]; A2 = Multiplier[1]; A3 = Multiplier[2]; A4 = Multiplier[3];
  //   A5 = Multiplier[4]; A6 = Multiplier[5]; A7 = Multiplier[6]; A8 = Multiplier[7]; A9 = Multiplier[8];
  //   A10 = Multiplier[9]; A11 = Multiplier[10]; A12 = Multiplier[11]; A13 = Multiplier[12]; A14 = Multiplier[13];
  //   A15 = Multiplier[14]; A16 = Multiplier[15]; O1 = Output[0]; O16_31[15:0] = Output[30:15]; O32 = Output[31]
endmodule

// ALU
module _32_bit_6_functions_ALU (
  input  Carry_in,
  input  [31:0] A_Multiplier,
  input  [31:0] B_Multiplicand,
  input  B_invert,
  input  A_invert,
  input  F1,
  input  F0,
  output Zero_flag,
  output [31:0] Output,
  output Carry_Out
);

  wire or_1_out;
  wire [2:0] alu_control_1_o0;
  wire [31:0] Multiplication_Unit_output, n32_bit_alu_1_output;

  _32_bit_ALU u_32_bit_alu_1 (
    .A(A_Multiplier), .B(B_Multiplicand), .Carry_in(Carry_in), .Select_Bits(alu_control_1_o0),
    .Output(n32_bit_alu_1_output), .Carry_out(Carry_Out), .B_invert(B_invert), .A_invert(A_invert));
  _16_bit_by_16_bit_Multiplication_Unit Multiplication_Unit (
    .Multiplicand(B_Multiplicand[15:0]), .Multiplier(A_Multiplier[15:0]), .Output(Multiplication_Unit_output));
  ALU_Control alu_control_1 (
    .B_invert(B_invert), .A_invert(A_invert), .F1(F1), .F0(F0), .O2(alu_control_1_o0[2]),
    .O1(alu_control_1_o0[1]), .O0(alu_control_1_o0[0]));
  Multiplexer #(.select(3), .width(32), .enable("false")) multiplexer_1 (
    .in0(n32_bit_alu_1_output), .in1(n32_bit_alu_1_output), .in2(n32_bit_alu_1_output),
    .in3(n32_bit_alu_1_output), .in4(n32_bit_alu_1_output), .in5(n32_bit_alu_1_output),
    .in6(n32_bit_alu_1_output), .in7(Multiplication_Unit_output), .out(Output), .sel(alu_control_1_o0));
  or or_1 (or_1_out, Output[0], Output[1], Output[2], Output[3], Output[4], Output[5], Output[6], Output[7], Output[8], Output[9], Output[10], Output[11], Output[12], Output[13], Output[14], Output[15], Output[16], Output[17], Output[18], Output[19], Output[20], Output[21], Output[22], Output[23], Output[24], Output[25], Output[26], Output[27], Output[28], Output[29], Output[30], Output[31]);
  not not_1 (Zero_flag, or_1_out);
endmodule

// Control Unit
module ALU_Control (
  input  B_invert,
  input  A_invert,
  input  F1,
  input  F0,
  output O2,
  output O1,
  output O0
);

  wire A_invert_invert, and_1_out, and_2_out, and_3_out, and_4_out, and_5_out, and_6_out, and_7_out,
       and_8_out, B_invert_invert, F0_invert, F1_invert, xor_1_out, xor_2_out, xor_3_out, xor_4_out;

  not not_1 (B_invert_invert, B_invert);
  not not_2 (A_invert_invert, A_invert);
  not not_3 (F1_invert, F1);
  not not_4 (F0_invert, F0);
  xor xor_1 (xor_1_out, B_invert, F1);
  xor xor_2 (xor_2_out, B_invert_invert, A_invert);
  and and_1 (and_1_out, F1_invert, F0_invert);
  xor xor_3 (xor_3_out, B_invert, A_invert);
  and and_2 (and_2_out, B_invert, F1_invert);
  and and_3 (and_3_out, B_invert_invert, F0);
  and and_4 (and_4_out, F0_invert, F1);
  xor xor_4 (xor_4_out, B_invert, F1);
  and and_5 (and_5_out, B_invert_invert, A_invert);
  and and_6 (and_6_out, F1_invert, F0_invert);
  and and_7 (and_7_out, A_invert, F1, F0_invert);
  and and_8 (and_8_out, F1, F0, A_invert_invert);
  or or_1 (O0, xor_4_out, and_5_out, and_6_out, and_7_out, and_8_out);
  or or_2 (O2, xor_1_out, xor_2_out, and_1_out);
  or or_3 (O1, xor_3_out, and_2_out, and_3_out, and_4_out);
endmodule

// Reg
module _32_bit_register (
  input  [31:0] Write_Data,
  input  [4:0] Read_Register_1__RS,
  input  [4:0] Read_Register_2__RT,
  input  Reg_Write,
  input  Clock,
  input  [4:0] Write_Register__RD,
  output [31:0] Read_Data_1,
  output [31:0] Read_Data_2
);

  wire and_1_out, and_2_out, and_3_out, and_4_out, and_5_out, and_6_out, and_7_out, and_8_out, and_9_out,
       and_10_out, and_11_out, and_12_out, and_13_out, and_14_out, and_15_out, and_16_out, and_17_out,
       and_18_out, and_19_out, and_20_out, and_21_out, and_22_out, and_23_out, and_24_out, and_25_out,
       and_26_out, and_27_out, and_28_out, and_29_out, and_30_out, and_31_out, and_32_out, decoder_1_out0,
       decoder_1_out1, decoder_1_out2, decoder_1_out3, decoder_1_out4, decoder_1_out5, decoder_1_out6,
       decoder_1_out7, decoder_1_out8, decoder_1_out9, decoder_1_out10, decoder_1_out11, decoder_1_out12,
       decoder_1_out13, decoder_1_out14, decoder_1_out15;
  wire [15:0] decoder_1_out16;
  wire [31:0] a0_4_q, a1_5_q, a2_6_q, a3_7_q, at_1_q, fp_30_q, gp_28_q, k0_26_q, k1_27_q, ra_31_q, s0_16_q,
       s1_17_q, s2_18_q, s3_19_q, s4_20_q, s5_21_q, s6_22_q, s7_23_q, sp_29_q, t0_8_q, t1_9_q, t2_10_q,
       t3_11_q, t4_12_q, t5_13_q, t6_14_q, t7_15_q, t8_24_q, t9_25_q, v0_2_q, v1_3_q, zero_0_q;

  Decoder #(.select(5), .enable("false")) decoder_1 (
    .out0(decoder_1_out0), .out1(decoder_1_out1), .out2(decoder_1_out2), .out3(decoder_1_out3),
    .out4(decoder_1_out4), .out5(decoder_1_out5), .out6(decoder_1_out6), .out7(decoder_1_out7),
    .out8(decoder_1_out8), .out9(decoder_1_out9), .out10(decoder_1_out10), .out11(decoder_1_out11),
    .out12(decoder_1_out12), .out13(decoder_1_out13), .out14(decoder_1_out14), .out15(decoder_1_out15),
    .out16(decoder_1_out16[0]), .out17(decoder_1_out16[1]), .out18(decoder_1_out16[2]),
    .out19(decoder_1_out16[3]), .out20(decoder_1_out16[4]), .out21(decoder_1_out16[5]),
    .out22(decoder_1_out16[6]), .out23(decoder_1_out16[7]), .out24(decoder_1_out16[8]),
    .out25(decoder_1_out16[9]), .out26(decoder_1_out16[10]), .out27(decoder_1_out16[11]),
    .out28(decoder_1_out16[12]), .out29(decoder_1_out16[13]), .out30(decoder_1_out16[14]),
    .out31(decoder_1_out16[15]), .sel(Write_Register__RD));
  and and_1 (and_1_out, decoder_1_out16[15], Reg_Write);
  and and_2 (and_2_out, decoder_1_out15, Reg_Write);
  and and_3 (and_3_out, decoder_1_out16[0], Reg_Write);
  and and_4 (and_4_out, decoder_1_out16[1], Reg_Write);
  and and_5 (and_5_out, decoder_1_out16[2], Reg_Write);
  and and_6 (and_6_out, decoder_1_out16[3], Reg_Write);
  and and_7 (and_7_out, decoder_1_out16[4], Reg_Write);
  and and_8 (and_8_out, decoder_1_out16[5], Reg_Write);
  and and_9 (and_9_out, decoder_1_out16[6], Reg_Write);
  and and_10 (and_10_out, decoder_1_out16[7], Reg_Write);
  and and_11 (and_11_out, decoder_1_out16[8], Reg_Write);
  and and_12 (and_12_out, decoder_1_out16[9], Reg_Write);
  and and_13 (and_13_out, decoder_1_out16[10], Reg_Write);
  and and_14 (and_14_out, decoder_1_out16[11], Reg_Write);
  and and_15 (and_15_out, decoder_1_out16[12], Reg_Write);
  and and_16 (and_16_out, decoder_1_out16[13], Reg_Write);
  and and_17 (and_17_out, decoder_1_out16[14], Reg_Write);
  and and_18 (and_18_out, decoder_1_out0, Reg_Write);
  and and_19 (and_19_out, decoder_1_out1, Reg_Write);
  and and_20 (and_20_out, decoder_1_out2, Reg_Write);
  and and_21 (and_21_out, decoder_1_out3, Reg_Write);
  and and_22 (and_22_out, decoder_1_out4, Reg_Write);
  and and_23 (and_23_out, decoder_1_out5, Reg_Write);
  and and_24 (and_24_out, decoder_1_out6, Reg_Write);
  and and_25 (and_25_out, decoder_1_out7, Reg_Write);
  and and_26 (and_26_out, decoder_1_out8, Reg_Write);
  and and_27 (and_27_out, decoder_1_out9, Reg_Write);
  and and_28 (and_28_out, decoder_1_out10, Reg_Write);
  and and_29 (and_29_out, decoder_1_out11, Reg_Write);
  and and_30 (and_30_out, decoder_1_out12, Reg_Write);
  and and_31 (and_31_out, decoder_1_out13, Reg_Write);
  and and_32 (and_32_out, decoder_1_out14, Reg_Write);
  Register #(.width(32)) s0_16 (.D(Write_Data), .en(and_3_out), .Q(s0_16_q), .clk(Clock));  // open: clr
  Register #(.width(32)) s1_17 (.D(Write_Data), .en(and_4_out), .Q(s1_17_q), .clk(Clock));  // open: clr
  Register #(.width(32)) s2_18 (.D(Write_Data), .en(and_5_out), .Q(s2_18_q), .clk(Clock));  // open: clr
  Register #(.width(32)) s3_19 (.D(Write_Data), .en(and_6_out), .Q(s3_19_q), .clk(Clock));  // open: clr
  Register #(.width(32)) s4_20 (.D(Write_Data), .en(and_7_out), .Q(s4_20_q), .clk(Clock));  // open: clr
  Register #(.width(32)) s5_21 (.D(Write_Data), .en(and_8_out), .Q(s5_21_q), .clk(Clock));  // open: clr
  Register #(.width(32)) s6_22 (.D(Write_Data), .en(and_9_out), .Q(s6_22_q), .clk(Clock));  // open: clr
  Register #(.width(32)) s7_23 (.D(Write_Data), .en(and_10_out), .Q(s7_23_q), .clk(Clock));  // open: clr
  Register #(.width(32)) t8_24 (.D(Write_Data), .en(and_11_out), .Q(t8_24_q), .clk(Clock));  // open: clr
  Register #(.width(32)) t9_25 (.D(Write_Data), .en(and_12_out), .Q(t9_25_q), .clk(Clock));  // open: clr
  Register #(.width(32)) k0_26 (.D(Write_Data), .en(and_13_out), .Q(k0_26_q), .clk(Clock));  // open: clr
  Register #(.width(32)) k1_27 (.D(Write_Data), .en(and_14_out), .Q(k1_27_q), .clk(Clock));  // open: clr
  Register #(.width(32)) gp_28 (.D(Write_Data), .en(and_15_out), .Q(gp_28_q), .clk(Clock));  // open: clr
  Register #(.width(32)) sp_29 (.D(Write_Data), .en(and_16_out), .Q(sp_29_q), .clk(Clock));  // open: clr
  Register #(.width(32)) fp_30 (.D(Write_Data), .en(and_17_out), .Q(fp_30_q), .clk(Clock));  // open: clr
  Register #(.width(32)) ra_31 (.D(Write_Data), .en(and_1_out), .Q(ra_31_q), .clk(Clock));  // open: clr
  Register #(.width(32)) zero_0 (.D(Write_Data), .en(and_18_out), .Q(zero_0_q), .clk(Clock));  // open: clr
  Register #(.width(32)) at_1 (.D(Write_Data), .en(and_19_out), .Q(at_1_q), .clk(Clock));  // open: clr
  Register #(.width(32)) v0_2 (.D(Write_Data), .en(and_20_out), .Q(v0_2_q), .clk(Clock));  // open: clr
  Register #(.width(32)) v1_3 (.D(Write_Data), .en(and_21_out), .Q(v1_3_q), .clk(Clock));  // open: clr
  Register #(.width(32)) a0_4 (.D(Write_Data), .en(and_22_out), .Q(a0_4_q), .clk(Clock));  // open: clr
  Register #(.width(32)) a1_5 (.D(Write_Data), .en(and_23_out), .Q(a1_5_q), .clk(Clock));  // open: clr
  Register #(.width(32)) a2_6 (.D(Write_Data), .en(and_24_out), .Q(a2_6_q), .clk(Clock));  // open: clr
  Register #(.width(32)) a3_7 (.D(Write_Data), .en(and_25_out), .Q(a3_7_q), .clk(Clock));  // open: clr
  Register #(.width(32)) t0_8 (.D(Write_Data), .en(and_26_out), .Q(t0_8_q), .clk(Clock));  // open: clr
  Register #(.width(32)) t1_9 (.D(Write_Data), .en(and_27_out), .Q(t1_9_q), .clk(Clock));  // open: clr
  Register #(.width(32)) t2_10 (.D(Write_Data), .en(and_28_out), .Q(t2_10_q), .clk(Clock));  // open: clr
  Register #(.width(32)) t3_11 (.D(Write_Data), .en(and_29_out), .Q(t3_11_q), .clk(Clock));  // open: clr
  Register #(.width(32)) t4_12 (.D(Write_Data), .en(and_30_out), .Q(t4_12_q), .clk(Clock));  // open: clr
  Register #(.width(32)) t5_13 (.D(Write_Data), .en(and_31_out), .Q(t5_13_q), .clk(Clock));  // open: clr
  Register #(.width(32)) t6_14 (.D(Write_Data), .en(and_32_out), .Q(t6_14_q), .clk(Clock));  // open: clr
  Register #(.width(32)) t7_15 (.D(Write_Data), .en(and_2_out), .Q(t7_15_q), .clk(Clock));  // open: clr
  Multiplexer #(.select(5), .width(32), .enable("false")) multiplexer_1 (
    .in0(zero_0_q), .in1(at_1_q), .in2(v0_2_q), .in3(v1_3_q), .in4(a0_4_q), .in5(a1_5_q), .in6(a2_6_q),
    .in7(a3_7_q), .in8(t0_8_q), .in9(t1_9_q), .in10(t2_10_q), .in11(t3_11_q), .in12(t4_12_q), .in13(t5_13_q),
    .in14(t6_14_q), .in15(t7_15_q), .in16(s0_16_q), .in17(s1_17_q), .in18(s2_18_q), .in19(s3_19_q),
    .in20(s4_20_q), .in21(s5_21_q), .in22(s6_22_q), .in23(s7_23_q), .in24(t8_24_q), .in25(t9_25_q),
    .in26(k0_26_q), .in27(k1_27_q), .in28(gp_28_q), .in29(sp_29_q), .in30(fp_30_q), .in31(ra_31_q),
    .out(Read_Data_1), .sel(Read_Register_1__RS));
  Multiplexer #(.select(5), .width(32), .enable("false")) multiplexer_2 (
    .in0(zero_0_q), .in1(at_1_q), .in2(v0_2_q), .in3(v1_3_q), .in4(a0_4_q), .in5(a1_5_q), .in6(a2_6_q),
    .in7(a3_7_q), .in8(t0_8_q), .in9(t1_9_q), .in10(t2_10_q), .in11(t3_11_q), .in12(t4_12_q), .in13(t5_13_q),
    .in14(t6_14_q), .in15(t7_15_q), .in16(s0_16_q), .in17(s1_17_q), .in18(s2_18_q), .in19(s3_19_q),
    .in20(s4_20_q), .in21(s5_21_q), .in22(s6_22_q), .in23(s7_23_q), .in24(t8_24_q), .in25(t9_25_q),
    .in26(k0_26_q), .in27(k1_27_q), .in28(gp_28_q), .in29(sp_29_q), .in30(fp_30_q), .in31(ra_31_q),
    .out(Read_Data_2), .sel(Read_Register_2__RT));
endmodule

module Main_Control (
  input  [5:0] Opcode,
  output RgtDst,
  output ALUSrc,
  output MemtoReg,
  output RegWrite,
  output MemRead,
  output MemWrite,
  output Branch,
  output ALUOp1,
  output ALUOp0
);

  wire not_1_out, not_2_out, not_3_out, not_4_out, not_5_out, not_6_out;

  not not_1 (not_1_out, Opcode[0]);
  not not_2 (not_2_out, Opcode[1]);
  not not_3 (not_3_out, Opcode[2]);
  not not_4 (not_4_out, Opcode[3]);
  not not_5 (not_5_out, Opcode[4]);
  not not_6 (not_6_out, Opcode[5]);
  and and_1 (ALUOp1, not_1_out, not_2_out, not_3_out, not_4_out, not_5_out, not_6_out);
  and and_2 (MemRead, Opcode[0], Opcode[1], not_3_out, not_4_out, not_5_out, Opcode[5]);
  and and_3 (MemWrite, Opcode[0], Opcode[1], not_3_out, Opcode[3], not_5_out, Opcode[5]);
  and and_4 (ALUOp0, not_1_out, not_2_out, Opcode[2], not_4_out, not_5_out, not_6_out);
  or or_1 (ALUSrc, MemRead, MemWrite);
  or or_2 (RegWrite, ALUOp1, MemRead);

  assign Branch = ALUOp0;
  assign MemtoReg = MemRead;
  assign RgtDst = ALUOp1;
endmodule

module Single_Cycle_Datapath (
  input  Carry_in,
  input  Clock,
  input  Clear,
  input  Write_on_RD,
  input  [5:0] Bin_Ain_F1_F0,
  input  Clear_Memory,
  input  Clock_2,
  output out_8,
  output out_9,
  output [31:0] Value_after_shfing_2_to_the_left,
  output [31:0] Write_data,
  output Carry_out,
  output [5:0] Opcode,
  output [31:0] Instruction,
  output [4:0] RS,
  output [4:0] RT,
  output [4:0] RD,
  output [31:0] Read_Data_2,
  output [31:0] Read_Data_1,
  output [5:0] Function,
  output [31:0] Write_data_2
);

  wire and_1_out, main_control_1_alusrc, main_control_1_branch, main_control_1_memread,
       main_control_1_memtoreg, main_control_1_memwrite, main_control_1_regwrite, main_control_1_rgtdst,
       n32_bit_6_functions_alu_1_zero_flag;
  wire [23:0] bit_extender_1_out, bit_extender_3_out;
  wire [31:0] adder_1_out, adder_2_out, bit_extender_2_out, multiplexer_2_out, multiplexer_3_out, PC_q,
       ram_1_data;

  Register #(.width(32)) PC (.D(multiplexer_3_out), .en(1'b1), .Q(PC_q), .clk(Clock), .clr(Clear));
  Bit_Extender #(.in_width(32), .out_width(24)) bit_extender_1 (.in(PC_q), .out(bit_extender_1_out));
  Adder #(.width(32)) adder_1 (.a(PC_q), .b(32'h4), .out(adder_1_out), .cin(1'b0), .cout(out_8));
  ROM #(.addrWidth(24), .dataWidth(32)) rom_1 (
    .addr(bit_extender_1_out), .data({Instruction[31:6], Function}), .sel(1'b1));
  Multiplexer #(.width(5), .enable("false")) multiplexer_1 (
    .in0(Instruction[20:16]), .in1(Instruction[15:11]), .out(RD), .sel(main_control_1_rgtdst));
  _32_bit_register u_32_bit_register_1 (
    .Write_Data(Write_data_2), .Read_Register_1__RS(Instruction[25:21]),
    .Read_Register_2__RT(Instruction[20:16]), .Reg_Write(main_control_1_regwrite), .Clock(Write_on_RD),
    .Write_Register__RD(RD), .Read_Data_1(Read_Data_1), .Read_Data_2(Read_Data_2));
  Main_Control main_control_1 (
    .Opcode(Instruction[31:26]), .RgtDst(main_control_1_rgtdst), .ALUSrc(main_control_1_alusrc),
    .MemtoReg(main_control_1_memtoreg), .RegWrite(main_control_1_regwrite), .MemRead(main_control_1_memread),
    .MemWrite(main_control_1_memwrite), .Branch(main_control_1_branch));  // open: ALUOp1, ALUOp0
  Multiplexer #(.width(32), .enable("false")) multiplexer_2 (
    .in0(Read_Data_2), .in1(bit_extender_2_out), .out(multiplexer_2_out), .sel(main_control_1_alusrc));
  assign bit_extender_2_out = {{16{Instruction[15]}}, {Instruction[15:6], Function}};  // Bit_Extender bit_extender_2
  _32_bit_6_functions_ALU u_32_bit_6_functions_alu_1 (
    .A_Multiplier(Read_Data_1), .B_Multiplicand(multiplexer_2_out), .F1(Bin_Ain_F1_F0[1]),
    .Output(Write_data), .Carry_Out(Carry_out), .A_invert(Bin_Ain_F1_F0[2]), .B_invert(Bin_Ain_F1_F0[3]),
    .F0(Bin_Ain_F1_F0[0]), .Carry_in(Carry_in), .Zero_flag(n32_bit_6_functions_alu_1_zero_flag));
  and and_1 (and_1_out, main_control_1_branch, n32_bit_6_functions_alu_1_zero_flag);
  Shifter #(.width(32)) shifter_1 (.in(bit_extender_2_out), .\dist (5'b00010), .out(Value_after_shfing_2_to_the_left));
  Adder #(.width(32)) adder_2 (
    .a(adder_1_out), .b(Value_after_shfing_2_to_the_left), .out(adder_2_out), .cin(1'b0), .cout(out_9));
  Bit_Extender #(.in_width(32), .out_width(24)) bit_extender_3 (.in(Write_data), .out(bit_extender_3_out));
  Multiplexer #(.width(32), .enable("false")) multiplexer_3 (
    .in0(adder_1_out), .in1(adder_2_out), .out(multiplexer_3_out), .sel(and_1_out));
  RAM #(.addrWidth(24), .dataWidth(32), .bus("separate")) ram_1 (
    .addr(bit_extender_3_out), .din(Read_Data_2), .data(ram_1_data), .str(main_control_1_memwrite),
    .sel(1'b1), .clk(Clock_2), .ld(main_control_1_memread), .clr(Clear_Memory));
  Multiplexer #(.width(32), .enable("false")) multiplexer_4 (
    .in0(Write_data), .in1(ram_1_data), .out(Write_data_2), .sel(main_control_1_memtoreg));

  assign Instruction[5:0] = Function;
  assign Opcode = Instruction[31:26];
  assign RS = Instruction[25:21];
  assign RT = Instruction[20:16];

  // Notes on the sheet:
  //   contents of rom_1 (hex, n*v repeats v):
  //   12a5820 0 0 0 ad280000 0 0 0 ad280006
  //   Make it 1 after executing Instruction for Data write on Register(RD)
  //   Enter 000001 here for add Operation
  //   Operation
  //   Add(00)
  //   Sw(04)
  //   MIPS Code
  //   add $t3, $t1, $t2
  //   sw  $t0, 0(t1)
  //   Machine Code
  //   000000 01001 01010 01011 00000 100000
  //   101011 01001 01000 00000 00000 000000
  //   Hex Value
  //   012A5820
  //   AD280000
endmodule
